# Fritzing sketch Sequencer_02 (saved by Fritzing 0.9.2b)
breadboards: 2
perfboards: 1

parts:
  U1 = mystery part, 16 pins [chip_label=74HC595]
  R1 = Resistor [tolerance=±5% resistance=1k package=THT]
  R2 = Resistor [tolerance=±5% resistance=1k package=THT]
  R3 = Resistor [tolerance=±5% resistance=1k package=THT]
  R4 = Resistor [tolerance=±5% resistance=1k package=THT]
  R5 = Resistor [tolerance=±5% resistance=1k package=THT]
  R6 = Resistor [tolerance=±5% resistance=1k package=THT]
  R7 = Resistor [tolerance=±5% resistance=1k package=THT]
  R8 = Resistor [tolerance=±5% resistance=1k package=THT]
  LED1 = LED - 3mm [color="Red (633nm)" package="3 mm [THT]"]
  LED2 = LED - 3mm [color="Red (633nm)" package="3 mm [THT]"]
  LED3 = LED - 3mm [color="Red (633nm)" package="3 mm [THT]"]
  LED4 = LED - 3mm [color="Red (633nm)" package="3 mm [THT]"]
  LED5 = LED - 3mm [color="Red (633nm)" package="3 mm [THT]"]
  LED6 = LED - 3mm [color="Red (633nm)" package="3 mm [THT]"]
  LED7 = LED - 3mm [color="Red (633nm)" package="3 mm [THT]"]
  LED8 = LED - 3mm [color="Red (633nm)" package="3 mm [THT]"]
  C1 = Ceramic Capacitor [capacitance=100nF package="100 mil [THT, multilayer]"]
  U2 = atmega168 [package=dip]
  C2 = Ceramic Capacitor [capacitance=100nF package="100 mil [THT, multilayer]"]
  パーツ1 = Arduino Ethernet Shield (Rev3)
  R9 = Rotary Potentiometer (Small) [maximum_resistance=100kΩ package=THT]
  R10 = Rotary Potentiometer (Small) [maximum_resistance=100kΩ package=THT]
  S1 = Pushbutton [package=THT]
  S2 = Pushbutton [package="[THT]"]
  S3 = Pushbutton [package="[THT]"]
  S4 = Pushbutton [package="[THT]"]
  S5 = Pushbutton [package="[THT]"]
  S6 = Pushbutton [package="[THT]"]
  S7 = Pushbutton [package="[THT]"]
  S8 = Pushbutton [package="[THT]"]
  S9 = Pushbutton [package="[THT]"]
  R11 = Resistor [tolerance=±5% resistance=1k package=THT]
  R12 = Resistor [tolerance=±5% resistance=1k package=THT]
  LED9 = LED - 3mm [color="Red (633nm)" package="3 mm [THT]"]
  LED10 = LED - 3mm [color="Red (633nm)" package="3 mm [THT]"]
  S10 = Pushbutton [package="[THT]"]
  R13 = Resistor [tolerance=±5% resistance=1k package=THT]
  R14 = Resistor [tolerance=±5% resistance=2.2k package=THT]
  RE1 = Rotary Encoder [package=THT]
  R15 = Resistor [tolerance=±5% resistance=220 package=THT]
  LED11 = LED - 3mm [color="Yellow (595nm)" package="3 mm [THT]"]

nets:
  N1: U1.pin1, R3.Pin_0
  N2: U1.pin2, R4.Pin_0
  N3: U1.pin3, R5.Pin_0
  N4: U1.pin4, R6.Pin_0
  N5: U1.pin5, R7.Pin_0
  N6: U1.pin6, R1.Pin_0
  N7: U1.pin7, R8.Pin_0
  N8: U1.pin8, U2.GND#7, C2.1, LED9.cathode, LED10.cathode, S10.Pin_1, S10.Pin_2, R14.Pin_1
  N9: U1.pin10, U1.pin16, C1.1, パーツ1.5V, R9.leg2, R10.leg2
  N10: U1.pin11, U2.A0
  N11: U1.pin12, U2.D13
  N12: U1.pin13, LED1.cathode, LED2.cathode, LED3.cathode, LED4.cathode, LED5.cathode, LED6.cathode, LED7.cathode, LED8.cathode, C1.0, パーツ1.GND, R9.leg1, R10.leg1, S1.leg0, LED11.cathode
  N13: U1.pin14, U2.D12
  N14: U1.pin15, R2.Pin_0
  N15: R1.Pin_1, LED7.anode
  N16: R2.Pin_1, LED1.anode
  N17: R3.Pin_1, LED2.anode
  N18: R4.Pin_1, LED3.anode
  N19: R5.Pin_1, LED4.anode
  N20: R6.Pin_1, LED5.anode
  N21: R7.Pin_1, LED6.anode
  N22: R8.Pin_1, LED8.anode
  N23: U2.RESET, R13.Pin_1, R14.Pin_0
  N24: U2.VCC, C2.0
  N25: U2.D6_(PWM), R11.Pin_0
  N26: U2.D7, R12.Pin_0
  N27: U2.D8, S10.Pin_3, S10.Pin_4
  N28: U2.D9_(PWM), S1.leg1
  N29: U2.D10_(PWM), RE1.EncoderPinB
  N30: U2.D11_(PWM), RE1.EncoderPinA
  N31: U2.A1, R10.wiper
  N32: U2.A2, R9.wiper
  N33: U2.A3, R15.Pin_0
  N34: U2.A4, パーツ1.A4/SDA
  N35: U2.A5, パーツ1.A5/SCL
  N36: パーツ1.D2, R13.Pin_0
  N37: S2.Pin_1, S2.Pin_2
  N38: S2.Pin_3, S2.Pin_4
  N39: S3.Pin_1, S3.Pin_2
  N40: S3.Pin_3, S3.Pin_4
  N41: S4.Pin_1, S4.Pin_2
  N42: S4.Pin_3, S4.Pin_4
  N43: S5.Pin_1, S5.Pin_2
  N44: S5.Pin_3, S5.Pin_4
  N45: S6.Pin_1, S6.Pin_2
  N46: S6.Pin_3, S6.Pin_4
  N47: S7.Pin_1, S7.Pin_2
  N48: S7.Pin_3, S7.Pin_4
  N49: S8.Pin_1, S8.Pin_2
  N50: S8.Pin_3, S8.Pin_4
  N51: S9.Pin_1, S9.Pin_2
  N52: S9.Pin_3, S9.Pin_4
  N53: R11.Pin_1, LED9.anode
  N54: R12.Pin_1, LED10.anode
  N55: R15.Pin_1, LED11.anode
